# Fritzing sketch programmer_reminder (saved by Fritzing 0.9.4)
breadboards: 1

parts:
  Part1 = Arduino Uno (Rev3)
  M1 = BME280
  Part2 = BH1750
  OLED1 = OLED 128x64 I2C Monochrome Display
  R5 = Resistor [tolerance=±5% resistance=220 package="2010 [SMD]"]
  J2 = Generic female header - 3 pins [form="♀ (female)" package=THT]
  J3 = Generic female header - 3 pins [form="♀ (female)" package=THT]
  J4 = Generic female header - 3 pins [form="♀ (female)" package=THT]
  Piezo1 = Piezo Speaker - PC Mount [part_number=COM-07950]

nets:
  N1: Part1.A4/SDA, M1.SDA, Part2.SDA, OLED1.SDA
  N2: Part1.A5/SCL, M1.SCL, Part2.SCL, OLED1.SCK
  N3: Part1.D8, R5.Pin_0
  N4: Part1.D2, J2.pin2
  N5: Part1.D3_PWM, J3.pin2
  N6: Part1.D4, J4.pin2
  5V: Part1.5V, M1.VIN, Part2.VCC, OLED1.VDD, J2.pin1, J3.pin1, J4.pin1
  GND: Part1.GND, M1.GND, Part2.GND, OLED1.GND, J2.pin3, J3.pin3, J4.pin3, Piezo1.GND
  N7: R5.Pin_1, Piezo1.VCC

custom parts:
  BME280: Temperature Humidity Barometric presure Sensor
  BH1750: Light Sensor
  Generic female header - 3 pins: Generic female header
  Piezo Speaker - PC Mount: This is a small 12mm round speaker that operates around the audible 2kHz range. You can use these speakers to create simple music or user interfaces. Each speaker is PTH solderable and requires an operating voltage of 3.5-5V with a mean current of 35mA max. These speakers also have a typical sound output of 95 dBA and a coil resistance of 42 ±6.3 ohms.
